# Fritzing sketch Type-X (saved by Fritzing 0.9.3b)
circuit board: 6cm x 16cm
breadboards: 1

parts:
  MoIC1 = TA7291P [package=HSIP10-P-2.54(THT)]
  MoIC2 = TA7291P [package=HSIP10-P-2.54(THT)]
  M2 = DC Motor
  M1 = DC Motor
  CPU = Arduino Nano (Rev3.0)
  Gnd- = Header 1 [package=1x01_offset]
  Vcc+ = Header 1 [package=1x01_offset]
  Bt1 = female pin header, 4 pins [form="♀ (female)"]
  PW = female pin header, 3 pins [form="♀ (female)"]
  S1 = SWITCH-MOMENTARY-2 [package=tactile-pth]

nets:
  GND: MoIC1.GND, MoIC2.GND, CPU.GND, Gnd-.1, Bt1.pin3, S1.2
  N1: MoIC1.OUT1, M1.pin_1
  N2: MoIC1.Vref, CPU.D5
  N3: MoIC1.IN1, CPU.D9
  N4: MoIC1.IN2, CPU.D8
  N5: MoIC1.Vs, MoIC2.Vs, CPU.VIN, PW.pin2
  N6: MoIC1.OUT2, M1.pin_2
  N7: MoIC2.OUT1, MoIC2.OUT2, M2.pin_1, M2.pin_2
  N8: MoIC2.Vref, CPU.D3
  N9: MoIC2.IN1, CPU.D7
  N10: MoIC2.IN2, CPU.D6
  N11: CPU.D10, Bt1.pin2, S1.1
  N12: CPU.D11/MOSI, Bt1.pin1
  N13: CPU.5V, Bt1.pin4
  N14: Vcc+.1, PW.pin1

notes:
  Type-Z_Ver.0.2
  I
  O

custom parts:
  TA7291P: The IC are Full-Bridge Driver. 4 modes available (CW / CCW / STOP / BRAKE) and PWM control. Output current:1.0 A (AVE.) 2.0 A (PEAK)
