# Fritzing sketch spica (saved by Fritzing 0.9.3b)
circuit board: 6cm x 6cm
breadboards: 1

parts:
  U1 = ESP32S-HiLetgo [part_number=ESP32S-HiLetgo]
  IC1 = V_REG_LD1117VXX [package=78xxl]
  C1 = Ceramic Capacitor [capacitance=0.1µF voltage=6.3V package="100 mil [THT, multilayer]"]
  C2 = Electrolytic Capacitor [capacitance=100µF package="100 mil [THT, electrolytic]"]
  C3 = Electrolytic Capacitor [capacitance=1mF voltage=10V package="100 mil [THT, electrolytic]"]
  IC2 = AE-DRV8835-S [package="DIP (Dual Inline) [THT]"]
  R1 = Resistor [tolerance=±5% resistance=220 package=THT]
  M2 = DC Motor
  R2 = Trimmer Potentiometer [maximum_resistance=10kΩ package=THT]
  VCC2 = 4 x AAA Battery Mount
  M1 = DC Motor
  JP2 = M16 [package=1x16_machine-pin-header_lock.004]
  JP3 = Header 3 [package=molex-1x3_lock]
  JP4 = M16 [package=1x16_machine-pin-header_lock.004]
  JP5 = M16 [package=1x16_machine-pin-header_lock.004]
  JP6 = Header 3 [package=molex-1x3_lock]
  JP7 = Header 3 [package=molex-1x3_lock]

nets:
  N1: U1.3.3, IC1.OUT, C2.+, IC2.MODE, IC2.VCC, JP7.1
  N2: U1.EN, JP7.2
  N3: U1.GPIO36, JP7.3
  N4: U1.GPIO39, JP4.16
  N5: U1.GPIO34, R2.leg1, JP4.15
  N6: U1.GPIO35, JP4.14
  N7: U1.GPIO32, R2.leg2, JP4.13
  N8: U1.GPIO33, R2.wiper, JP4.12
  N9: U1.GPIO25, IC2.AIN1, JP4.11
  N10: U1.GPIO26, IC2.AIN2, JP4.10
  N11: U1.GPIO27, JP4.9
  N12: U1.GPIO14, JP4.8
  N13: U1.GPIO12, JP4.7
  GND: U1.GND, IC1.GND, C1.0, C2.-, C3.-, IC2.GND, VCC2.-, JP2.4, JP3.1, JP4.6, JP5.4, JP6.1
  N14: U1.GPIO13, JP4.5
  N15: U1.GPIO9, JP4.4
  N16: U1.GPIO10, JP4.3
  N17: U1.GPIO11, JP4.2
  N18: U1.VIN, JP4.1
  N19: U1.GPIO6, JP2.16, JP5.16
  N20: U1.GPIO7, JP2.15, JP5.15
  N21: U1.GPIO8, JP2.14, JP5.14
  N22: U1.GPIO15, JP2.13, JP5.13
  N23: U1.GPIO2, JP2.12, JP5.12
  N24: U1.GPIO0, JP2.11, JP5.11
  N25: U1.GPIO4, JP2.10, JP5.10
  N26: U1.GPIO16, IC2.BIN1, JP2.9, JP5.9
  N27: U1.GPIO17, IC2.BIN2, JP2.8, JP5.8
  N28: U1.GPIO5, JP2.7, JP5.7
  N29: U1.GPIO18, JP2.6, JP5.6
  N30: U1.GPIO19, JP2.5, JP5.5
  N31: U1.GPIO21, JP2.3, JP5.3
  N32: U1.GPIO3, JP2.2, JP5.2
  N33: U1.GPIO1, JP2.1, JP5.1
  N34: U1.GPIO22, JP3.3, JP6.3
  N35: U1.GPIO23, JP3.2, JP6.2
  N36: IC1.IN, C1.1, C3.+, R1.Pin_1
  N37: IC2.VM, R1.Pin_0, VCC2.+
  N38: IC2.AOUT1, M1.pin_1
  N39: IC2.AOUT2, M1.pin_2
  N40: IC2.BOUT1, M2.pin_1
  N41: IC2.BOUT2, M2.pin_2

notes:
  Spica Dev Rev1.0b
  USB

custom parts:
  ESP32S-HiLetgo: HiLetgo ESP-WROOM-32 ESP32 ESP-32S Development Board 2.4GHz Dual-Mode WiFi + Bluetooth Dual Cores Microcontroller The ESP32 integrated with Antenna switches, RF Balun, power amplifiers, low-noise amplifiers, filters, and management modules, and the entire solution occupies the least area of PCB. 2.4 GHz Wi-Fi plus Bluetooth dual-mode chip, with TSMC Ultra-low power consumption 40nm technology,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
  AE-DRV8835-S: A DRV8835 breakout board by Akizuki Denshi Tsusho Co.,Ltd.
